# Fritzing sketch schematics_prototype (saved by Fritzing 0.9.2b)
breadboards: 1

parts:
  IC1 = L293D [package=THT]
  M1 = DC Motor
  M2 = DC Motor
  VCC_battery = 4 x AAA Battery Mount
  J1 = Infrared Proximity Sensor
  J2 = Infrared Proximity Sensor
  Part1 = Arduino Uno (Rev3)

nets:
  N1: IC1.Enable_1, Part1.D11_PWM/MOSI
  N2: IC1.In_1, Part1.D8
  N3: IC1.Out_1_(_Controlled_by_Enable_1_), M2.pin_2
  GND: IC1.0V, VCC_battery.-, J1.GND, J2.GND, Part1.GND
  N4: IC1.Out_2_(_Controlled_by_Enable_1_), M2.pin_1
  N5: IC1.In_2, Part1.D9_PWM
  N6: IC1.+Vmotor, VCC_battery.+
  N7: IC1.Enable_2, Part1.D10_PWM/SS
  N8: IC1.In_3, Part1.D13/SCK
  N9: IC1.Out_3_(_Controlled_by_Enable_2_), M1.pin_2
  N10: IC1.Out_4_(_Controlled_by_Enable_2_), M1.pin_1
  N11: IC1.In_4, Part1.D12/MISO
  VCC: IC1.+V, J1.Vcc, J2.Vcc, Part1.5V
  N12: J1.Vout, Part1.D4
  N13: J2.Vout, Part1.D3_PWM
